# Fritzing sketch ClapSensor (saved by Fritzing 0.9.3b)
breadboards: 1

parts:
  RaspberryPi_Zero_W = Raspberry Pi Zero
  SoundSensor = Breakout Board for Electret Microphone
  LED = LED - 3mm [color="Red (633nm)" package="3 mm [THT]"]
  R1 = Resistor [tolerance=±5% resistance=150 package="2010 [SMD]"]

nets:
  N1: RaspberryPi_Zero_W.pin_2, SoundSensor.VCC
  N2: RaspberryPi_Zero_W.pin_6, RaspberryPi_Zero_W.pin_9, SoundSensor.GND, LED.cathode
  N3: RaspberryPi_Zero_W.pin_38, R1.Pin_1
  N4: RaspberryPi_Zero_W.pin_40, SoundSensor.AUD
  N5: LED.anode, R1.Pin_0
